// Logisim project LAB#1_Problem1.circ as structural Verilog: 1 circuit, main circuit main
module main (
  input  A,
  input  B,
  output Z0,
  output Z1,
  output Z2
);

  wire nand_1_out, nand_2_out, nand_3_out, nand_4_out;

  nand nand_1 (nand_1_out, A, B);
  nand nand_2 (nand_2_out, A, nand_1_out);
  nand nand_3 (nand_3_out, nand_1_out, B);
  nand nand_4 (nand_4_out, nand_2_out, nand_3_out);
  nand nand_5 (Z0, nand_2_out, nand_2_out);
  nand nand_6 (Z1, nand_4_out, nand_4_out);
  nand nand_7 (Z2, nand_3_out, nand_3_out);
endmodule
