// Logisim project LAB#1_Problem3.circ as structural Verilog: 1 circuit, main circuit main
module main (
  input  a3,
  input  a2,
  input  a1,
  input  a0
);

  wire and_1_out, and_2_out, and_3_out, and_4_out, and_5_out, and_6_out, and_7_out, and_8_out, and_9_out,
       and_10_out, and_11_out, and_12_out, and_13_out, and_14_out, and_15_out, and_16_out, and_17_out,
       and_18_out, and_19_out, and_20_out, and_21_out, and_22_out, and_23_out, and_24_out, and_25_out,
       and_26_out, and_27_out, and_28_out, and_29_out, and_30_out, and_31_out, and_32_out, and_33_out,
       and_34_out, and_35_out, and_36_out, and_37_out, and_38_out, and_39_out, and_40_out, and_41_out,
       not_1_out, not_2_out, not_3_out, not_4_out, not_5_out, not_6_out, not_7_out, not_8_out, not_9_out,
       not_10_out, not_11_out, not_12_out, not_13_out, not_14_out, not_15_out, not_16_out, not_17_out,
       not_18_out, not_19_out, not_20_out, not_21_out, not_22_out, not_23_out, not_24_out, not_25_out,
       not_26_out, not_27_out, not_28_out, not_29_out, not_30_out, not_31_out, not_32_out, not_33_out,
       not_34_out, not_35_out, not_36_out, not_37_out, not_38_out, not_39_out, not_40_out, not_41_out,
       not_42_out, not_43_out, not_44_out, not_45_out, not_46_out, not_47_out, not_48_out, not_49_out,
       or_1_out, or_2_out, or_3_out, or_4_out, or_5_out, or_6_out, or_7_out, or_8_out, or_9_out, or_10_out,
       or_11_out, or_12_out, or_13_out, or_14_out, or_15_out, or_16_out, or_17_out;

  and and_1 (and_1_out, a3, a1);
  and and_2 (and_2_out, a3, a2);
  not not_1 (not_1_out, a2);
  and and_3 (and_3_out, a3, not_1_out, not_2_out);
  not not_2 (not_2_out, a1);
  not not_3 (not_3_out, a3);
  and and_4 (and_4_out, not_3_out, a2);
  and and_5 (and_5_out, a2, a1);
  not not_4 (not_4_out, a3);
  and and_6 (and_6_out, not_4_out, a1);
  and and_7 (and_7_out, a3, a2, not_5_out);
  not not_5 (not_5_out, a1);
  or or_1 (or_1_out, and_1_out, and_2_out);
  or or_2 (or_2_out, and_4_out, and_5_out);
  or or_3 (or_3_out, and_6_out, and_7_out);
  not not_6 (not_6_out, or_2_out);
  not not_7 (not_7_out, a0);
  not not_8 (not_8_out, or_2_out);
  not not_9 (not_9_out, or_3_out);
  not not_10 (not_10_out, a0);
  not not_11 (not_11_out, or_3_out);
  not not_12 (not_12_out, or_2_out);
  not not_13 (not_13_out, a0);
  not not_14 (not_14_out, or_2_out);
  not not_15 (not_15_out, a0);
  not not_16 (not_16_out, or_3_out);
  not not_17 (not_17_out, or_2_out);
  not not_18 (not_18_out, a0);
  not not_19 (not_19_out, a0);
  not not_20 (not_20_out, or_3_out);
  not not_21 (not_21_out, a0);
  not not_22 (not_22_out, or_3_out);
  not not_23 (not_23_out, a0);
  not not_24 (not_24_out, or_2_out);
  not not_25 (not_25_out, or_3_out);
  not not_26 (not_26_out, a0);
  and and_8 (and_8_out, not_6_out, not_7_out);
  and and_9 (and_9_out, not_8_out, or_3_out);
  and and_10 (and_10_out, or_2_out, a0);
  not not_27 (not_27_out, or_2_out);
  or or_4 (or_4_out, not_27_out, and_11_out, and_12_out);
  and and_11 (and_11_out, not_9_out, not_10_out);
  and and_12 (and_12_out, or_3_out, a0);
  or or_5 (or_5_out, not_11_out, a0, or_2_out);
  and and_13 (and_13_out, not_12_out, not_13_out);
  and and_14 (and_14_out, not_14_out, or_3_out);
  and and_15 (and_15_out, or_3_out, not_15_out);
  and and_16 (and_16_out, or_2_out, not_16_out, a0);
  and and_17 (and_17_out, not_17_out, not_18_out);
  or or_6 (or_6_out, and_17_out, and_18_out);
  and and_18 (and_18_out, or_3_out, not_19_out);
  and and_19 (and_19_out, not_20_out, not_21_out);
  and and_20 (and_20_out, or_2_out, not_22_out);
  and and_21 (and_21_out, or_2_out, not_23_out);
  and and_22 (and_22_out, not_24_out, or_3_out);
  and and_23 (and_23_out, or_2_out, not_25_out);
  and and_24 (and_24_out, or_2_out, not_26_out);
  _7_Segment_Display u_7_segment_display_1 (
    .g(or_17_out), .f(or_16_out), .a(or_12_out), .b(or_13_out), .e(or_15_out), .d(or_14_out), .c(or_11_out));  // open: dp
  or or_7 (or_7_out, and_8_out, and_9_out, and_10_out, and_3_out);
  or or_8 (or_8_out, and_13_out, and_14_out, and_15_out, and_16_out);
  or or_9 (or_9_out, and_19_out, and_20_out, and_21_out, and_3_out);
  or or_10 (or_10_out, and_22_out, and_23_out, and_24_out, and_3_out);
  _7_Segment_Display u_7_segment_display_2 (
    .g(or_10_out), .f(or_9_out), .a(or_7_out), .b(or_4_out), .e(or_6_out), .d(or_8_out), .c(or_5_out));  // open: dp
  not not_28 (not_28_out, 1'b0);
  not not_29 (not_29_out, or_1_out);
  not not_30 (not_30_out, 1'b0);
  not not_31 (not_31_out, 1'b0);
  not not_32 (not_32_out, or_1_out);
  not not_33 (not_33_out, 1'b0);
  not not_34 (not_34_out, 1'b0);
  not not_35 (not_35_out, or_1_out);
  not not_36 (not_36_out, 1'b0);
  not not_37 (not_37_out, or_1_out);
  not not_38 (not_38_out, 1'b0);
  not not_39 (not_39_out, 1'b0);
  not not_40 (not_40_out, or_1_out);
  not not_41 (not_41_out, or_1_out);
  not not_42 (not_42_out, 1'b0);
  not not_43 (not_43_out, or_1_out);
  not not_44 (not_44_out, 1'b0);
  not not_45 (not_45_out, or_1_out);
  not not_46 (not_46_out, 1'b0);
  not not_47 (not_47_out, 1'b0);
  not not_48 (not_48_out, or_1_out);
  and and_25 (and_25_out, not_28_out, not_29_out);
  and and_26 (and_26_out, not_30_out, 1'b0);
  and and_27 (and_27_out, 1'b0, or_1_out);
  not not_49 (not_49_out, 1'b0);
  and and_28 (and_28_out, not_31_out, not_32_out);
  and and_29 (and_29_out, 1'b0, or_1_out);
  or or_11 (or_11_out, not_33_out, or_1_out, 1'b0);
  and and_30 (and_30_out, not_34_out, not_35_out);
  and and_31 (and_31_out, not_36_out, 1'b0);
  and and_32 (and_32_out, 1'b0, not_37_out);
  and and_33 (and_33_out, 1'b0, not_38_out, or_1_out);
  and and_34 (and_34_out, not_39_out, not_40_out);
  and and_35 (and_35_out, 1'b0, not_41_out);
  and and_36 (and_36_out, not_42_out, not_43_out);
  and and_37 (and_37_out, 1'b0, not_44_out);
  and and_38 (and_38_out, 1'b0, not_45_out);
  and and_39 (and_39_out, not_46_out, 1'b0);
  and and_40 (and_40_out, 1'b0, not_47_out);
  and and_41 (and_41_out, 1'b0, not_48_out);
  or or_12 (or_12_out, and_25_out, and_26_out, and_27_out, 1'b0);
  or or_13 (or_13_out, not_49_out, and_28_out, and_29_out);
  or or_14 (or_14_out, and_30_out, and_31_out, and_32_out, and_33_out);
  or or_15 (or_15_out, and_34_out, and_35_out);
  or or_16 (or_16_out, and_36_out, and_37_out, and_38_out, 1'b0);
  or or_17 (or_17_out, and_39_out, and_40_out, and_41_out, 1'b0);
endmodule
