// Logisim project LAB#2_up_down_counter_7_Segement.circ as structural Verilog: 1 circuit, main circuit main
module main (
  input  x3,
  input  x2,
  input  in_3
);

  wire A_q, and_1_out, and_2_out, and_3_out, and_4_out, and_5_out, and_6_out, and_7_out, and_8_out,
       and_9_out, and_10_out, and_11_out, and_12_out, and_13_out, and_14_out, and_15_out, and_16_out,
       and_17_out, B_q, CLK_out, not_1_out, not_2_out, not_3_out, not_4_out, not_5_out, not_6_out, not_7_out,
       not_8_out, not_9_out, not_10_out, not_11_out, not_12_out, not_13_out, not_14_out, not_15_out,
       not_16_out, not_17_out, not_18_out, not_19_out, not_20_out, not_21_out, not_22_out, not_23_out,
       not_24_out, not_25_out, or_1_out, or_2_out, or_3_out, or_4_out, or_5_out, or_6_out, or_7_out,
       xor_1_out, xor_2_out;

  Clock CLK (.out(CLK_out));
  not not_1 (not_1_out, in_3);
  xor xor_1 (xor_1_out, B_q, A_q);
  xor xor_2 (xor_2_out, not_1_out, xor_1_out);
  D_Flip_Flop A (.clk(CLK_out), .D(not_3_out), .Q(A_q));  // open: Qn, preset, en, reset
  D_Flip_Flop B (.clk(CLK_out), .D(not_2_out), .Q(B_q));  // open: Qn, preset, en, reset
  not not_2 (not_2_out, xor_2_out);
  not not_3 (not_3_out, A_q);
  not not_4 (not_4_out, x2);
  not not_5 (not_5_out, not_3_out);
  not not_6 (not_6_out, x2);
  not not_7 (not_7_out, not_2_out);
  not not_8 (not_8_out, not_3_out);
  not not_9 (not_9_out, not_2_out);
  not not_10 (not_10_out, x2);
  not not_11 (not_11_out, not_3_out);
  not not_12 (not_12_out, x2);
  not not_13 (not_13_out, not_3_out);
  not not_14 (not_14_out, not_2_out);
  not not_15 (not_15_out, x2);
  not not_16 (not_16_out, not_3_out);
  not not_17 (not_17_out, not_3_out);
  not not_18 (not_18_out, not_2_out);
  not not_19 (not_19_out, not_3_out);
  not not_20 (not_20_out, not_2_out);
  not not_21 (not_21_out, not_3_out);
  not not_22 (not_22_out, x2);
  not not_23 (not_23_out, not_2_out);
  not not_24 (not_24_out, not_3_out);
  and and_1 (and_1_out, not_4_out, not_5_out);
  and and_2 (and_2_out, not_6_out, not_2_out);
  and and_3 (and_3_out, x2, not_3_out);
  not not_25 (not_25_out, x2);
  and and_4 (and_4_out, not_7_out, not_8_out);
  and and_5 (and_5_out, not_2_out, not_3_out);
  or or_1 (or_1_out, not_9_out, not_3_out, x2);
  and and_6 (and_6_out, not_10_out, not_11_out);
  and and_7 (and_7_out, not_12_out, not_2_out);
  and and_8 (and_8_out, not_2_out, not_13_out);
  and and_9 (and_9_out, x2, not_14_out, not_3_out);
  and and_10 (and_10_out, not_15_out, not_16_out);
  and and_11 (and_11_out, not_2_out, not_17_out);
  and and_12 (and_12_out, not_18_out, not_19_out);
  and and_13 (and_13_out, x2, not_20_out);
  and and_14 (and_14_out, x2, not_21_out);
  and and_15 (and_15_out, not_22_out, not_2_out);
  and and_16 (and_16_out, x2, not_23_out);
  and and_17 (and_17_out, x2, not_24_out);
  or or_2 (or_2_out, and_1_out, and_2_out, and_3_out, x3);
  or or_3 (or_3_out, not_25_out, and_4_out, and_5_out);
  or or_4 (or_4_out, and_6_out, and_7_out, and_8_out, and_9_out);
  or or_5 (or_5_out, and_10_out, and_11_out);
  or or_6 (or_6_out, and_12_out, and_13_out, and_14_out, x3);
  or or_7 (or_7_out, and_15_out, and_16_out, and_17_out, x3);
  _7_Segment_Display u_7_segment_display_1 (
    .g(or_7_out), .f(or_6_out), .a(or_2_out), .b(or_3_out), .e(or_5_out), .d(or_4_out), .c(or_1_out));  // open: dp
endmodule
