// Logisim project LAB#3.circ as structural Verilog: 1 circuit, main circuit maincircuit
module maincircuit (
  input  _1000,
  input  _500
);

  wire A_q, and_1_out, and_2_out, and_3_out, and_4_out, and_5_out, and_6_out, and_7_out, and_8_out,
       and_9_out, and_10_out, and_11_out, and_12_out, and_13_out, and_14_out, and_15_out, and_16_out,
       and_17_out, and_18_out, and_19_out, and_20_out, B_q, C_q, clock_1_out, not_1_out, not_2_out,
       not_3_out, not_4_out, not_5_out, not_6_out, not_7_out, not_8_out, not_9_out, not_10_out, not_11_out,
       not_12_out, not_13_out, not_14_out, not_15_out, not_16_out, not_17_out, not_18_out, not_19_out,
       not_20_out, not_21_out, not_22_out, not_23_out, not_24_out, not_25_out, not_26_out, not_27_out,
       not_28_out, not_29_out, or_1_out, or_2_out, or_3_out, or_4_out, or_5_out, or_6_out, or_7_out,
       or_8_out, or_9_out;

  not not_1 (not_1_out, B_q);
  not not_2 (not_2_out, B_q);
  not not_3 (not_3_out, _1000);
  not not_4 (not_4_out, A_q);
  not not_5 (not_5_out, A_q);
  and and_1 (and_1_out, not_1_out, _1000);
  and and_2 (and_2_out, _1000, A_q);
  and and_3 (and_3_out, _500, not_2_out, A_q);
  and and_4 (and_4_out, not_3_out, B_q, not_4_out);
  not not_6 (not_6_out, A_q);
  not not_7 (not_7_out, B_q);
  not not_8 (not_8_out, _500);
  and and_5 (and_5_out, _1000, not_5_out, B_q);
  and and_6 (and_6_out, B_q, _500);
  and and_7 (and_7_out, _500, not_6_out);
  and and_8 (and_8_out, A_q, not_7_out, not_8_out);
  or or_1 (or_1_out, and_1_out, and_2_out, and_3_out, and_4_out);
  or or_2 (or_2_out, and_6_out, and_7_out, and_8_out);
  Clock clock_1 (.out(clock_1_out));
  D_Flip_Flop C (.clk(clock_1_out), .D(and_5_out), .Q(C_q));  // open: Qn, preset, en, reset
  D_Flip_Flop B (.clk(clock_1_out), .D(or_1_out), .Q(B_q));  // open: Qn, preset, en, reset
  D_Flip_Flop A (.clk(clock_1_out), .D(or_2_out), .Q(A_q));  // open: Qn, preset, en, reset
  and and_9 (and_9_out, B_q, A_q);
  or or_3 (or_3_out, C_q, and_9_out);
  LED Drink (.in(or_3_out));
  LED Change (.in(C_q));
  not not_9 (not_9_out, 1'b0);
  not not_10 (not_10_out, C_q);
  not not_11 (not_11_out, A_q);
  not not_12 (not_12_out, C_q);
  not not_13 (not_13_out, 1'b0);
  not not_14 (not_14_out, B_q);
  not not_15 (not_15_out, B_q);
  not not_16 (not_16_out, 1'b0);
  not not_17 (not_17_out, C_q);
  not not_18 (not_18_out, A_q);
  not not_19 (not_19_out, C_q);
  not not_20 (not_20_out, 1'b0);
  not not_21 (not_21_out, C_q);
  not not_22 (not_22_out, A_q);
  not not_23 (not_23_out, 1'b0);
  not not_24 (not_24_out, B_q);
  not not_25 (not_25_out, A_q);
  not not_26 (not_26_out, C_q);
  not not_27 (not_27_out, C_q);
  not not_28 (not_28_out, B_q);
  not not_29 (not_29_out, A_q);
  and and_10 (and_10_out, not_9_out, not_10_out, not_11_out);
  and and_11 (and_11_out, not_12_out, B_q);
  and and_12 (and_12_out, 1'b0, C_q);
  or or_4 (or_4_out, not_13_out, not_14_out, C_q);
  or or_5 (or_5_out, not_15_out, A_q, C_q, 1'b0);
  and and_13 (and_13_out, not_16_out, not_17_out, not_18_out);
  and and_14 (and_14_out, not_19_out, B_q);
  and and_15 (and_15_out, 1'b0, C_q);
  and and_16 (and_16_out, not_20_out, not_21_out, not_22_out);
  and and_17 (and_17_out, not_23_out, not_24_out, not_25_out);
  and and_18 (and_18_out, 1'b0, not_26_out);
  and and_19 (and_19_out, not_27_out, B_q);
  and and_20 (and_20_out, C_q, not_28_out, not_29_out);
  or or_6 (or_6_out, and_10_out, and_11_out, and_12_out);
  or or_7 (or_7_out, and_13_out, and_14_out, and_15_out);
  or or_8 (or_8_out, and_17_out, and_18_out);
  or or_9 (or_9_out, and_19_out, and_20_out, 1'b0);
  _7_Segment_Display u_7_segment_display_1 (
    .g(or_9_out), .f(or_8_out), .a(or_6_out), .b(or_4_out), .e(and_16_out), .d(or_7_out), .c(or_5_out));  // open: dp
endmodule
