// Logisim project Traffic Light Controller_2190416_안견힐.circ as structural Verilog: 6 circuits, main circuit Next_state
module main (
  input  V
);

  wire A_q, and_1_out, and_2_out, and_3_out, and_4_out, and_5_out, B_q, C_q, CLK_out, not_1_out, not_2_out,
       not_3_out, not_4_out, not_5_out, or_1_out, xor_1_out;

  and and_1 (and_1_out, B_q, C_q);
  xor xor_1 (xor_1_out, B_q, C_q);
  and and_2 (and_2_out, B_q, not_1_out);
  not not_1 (not_1_out, C_q);
  not not_2 (not_2_out, A_q);
  not not_3 (not_3_out, C_q);
  and and_3 (and_3_out, not_2_out, not_3_out, V);
  or or_1 (or_1_out, and_2_out, and_3_out);
  Clock CLK (.out(CLK_out));
  D_Flip_Flop A (.clk(CLK_out), .D(and_1_out), .Q(A_q));  // open: Qn, preset, en, reset
  D_Flip_Flop B (.clk(CLK_out), .D(xor_1_out), .Q(B_q));  // open: Qn, preset, en, reset
  D_Flip_Flop C (.clk(CLK_out), .D(or_1_out), .Q(C_q));  // open: Qn, preset, en, reset
  not not_4 (not_4_out, B_q);
  not not_5 (not_5_out, C_q);
  and and_4 (and_4_out, not_4_out, not_5_out);
  LED Green (.in(and_4_out));
  and and_5 (and_5_out, not_4_out, C_q);
  LED Yellow (.in(and_5_out));
  LED Red (.in(B_q));
endmodule

module Next_state (
  input  CLK,
  input  V,
  output B,
  output C
);

  wire A_q, and_1_out, and_2_out, and_3_out, not_1_out, not_2_out, not_3_out, or_1_out, xor_1_out;

  and and_1 (and_1_out, B, C);
  xor xor_1 (xor_1_out, B, C);
  and and_2 (and_2_out, B, not_1_out);
  not not_1 (not_1_out, C);
  not not_2 (not_2_out, A_q);
  not not_3 (not_3_out, C);
  and and_3 (and_3_out, not_2_out, not_3_out, V);
  or or_1 (or_1_out, and_2_out, and_3_out);
  D_Flip_Flop A (.clk(CLK), .D(and_1_out), .Q(A_q));  // open: Qn, preset, en, reset
  D_Flip_Flop u_B (.clk(CLK), .D(xor_1_out), .Q(B));  // open: Qn, preset, en, reset
  D_Flip_Flop u_C (.clk(CLK), .D(or_1_out), .Q(C));  // open: Qn, preset, en, reset
endmodule

module Output (
  input  B,
  input  C,
  output G,
  output Y,
  output R
);

  wire not_1_out, not_2_out;

  not not_1 (not_1_out, B);
  not not_2 (not_2_out, C);
  and and_1 (G, not_1_out, not_2_out);
  and and_2 (Y, not_1_out, C);

  assign R = B;
endmodule

module FSM (
  input  V
);

  wire CLK_out, Next_State_b, Next_State_c, Output_g, Output_r, Output_y;

  Clock CLK (.out(CLK_out));
  Next_state Next_State (.CLK(CLK_out), .V(V), .B(Next_State_b), .C(Next_State_c));
  Output Output (.B(Next_State_b), .C(Next_State_c), .G(Output_g), .Y(Output_y), .R(Output_r));
  LED Red (.in(Output_r));
  LED Yellow (.in(Output_y));
  LED Green (.in(Output_g));
endmodule

module Updating_Next_State (
  input  B,
  input  C,
  input  A,
  input  V,
  output A_plus,
  output B_plus,
  output C_plus
);

  wire and_2_out, and_3_out, not_1_out, not_2_out, not_3_out;

  and and_1 (A_plus, B, C);
  xor xor_1 (B_plus, B, C);
  and and_2 (and_2_out, B, not_1_out);
  not not_1 (not_1_out, C);
  not not_2 (not_2_out, A);
  and and_3 (and_3_out, not_2_out, not_3_out, V);
  not not_3 (not_3_out, C);
  or or_1 (C_plus, and_2_out, and_3_out);
endmodule

module FSM_2 (
  input  V
);

  wire CLK_out, d_ff_1_q, d_ff_2_q, d_ff_3_q, Next_State_a_plus, Next_State_b_plus, Next_State_c_plus,
       Output_g, Output_r, Output_y;

  Clock CLK (.out(CLK_out));
  Output Output (.B(d_ff_2_q), .C(d_ff_3_q), .G(Output_g), .Y(Output_y), .R(Output_r));
  Updating_Next_State Next_State (
    .B(d_ff_2_q), .C(d_ff_3_q), .A(d_ff_1_q), .V(V), .A_plus(Next_State_a_plus), .B_plus(Next_State_b_plus),
    .C_plus(Next_State_c_plus));
  D_Flip_Flop d_ff_1 (.clk(CLK_out), .D(Next_State_a_plus), .Q(d_ff_1_q));  // open: Qn, preset, en, reset
  D_Flip_Flop d_ff_2 (.clk(CLK_out), .D(Next_State_b_plus), .Q(d_ff_2_q));  // open: Qn, preset, en, reset
  D_Flip_Flop d_ff_3 (.clk(CLK_out), .D(Next_State_c_plus), .Q(d_ff_3_q));  // open: Qn, preset, en, reset
  LED Yellow (.in(Output_y));
  LED Red (.in(Output_r));
  LED Green (.in(Output_g));

  // Notes on the sheet:
  //   C
  //   B
  //   A
  //   B
  //   C
  //   C+
  //   B+
  //   A+
  //   C
  //   B
  //   A
  //   C+
  //   B+
  //   A+
endmodule
